# Fritzing sketch circuit (saved by Fritzing 1.0.3b)
stripboards: 2

parts:
  Mod1 = Raspberry Pi 4B
  J1 = Screw terminal - 2 pins [package=THT]
  J2 = Screw terminal - 2 pins [package=THT]
  J3 = Screw terminal - 2 pins [package=THT]
  J4 = Screw terminal - 2 pins [package=THT]
  Gravity_Digital_Microwave_Sensor1 = Gravity: Digital Microwave Sensor [package=sot23-3]
  M1 = RioRand LM2596
  USB_C_Plug1 = USB C Plug [package=micro-b-ra-th]
  12V_LED_Array1 = 12V LED Array
  R2 = Resistor [tolerance=±5% resistance=220 package="2512 [SMD]"]
  Q2 = NPN-Transistor [package="TO92 [THT]"]
  J5 = Power Jack [package=power_jack_combo]

nets:
  5V: Mod1.5V, Gravity_Digital_Microwave_Sensor1.VCC
  GND: Mod1.GND, Gravity_Digital_Microwave_Sensor1.GND
  N1: Mod1.GPIO27, Gravity_Digital_Microwave_Sensor1.SDO
  N2: Mod1.GPIO23, R2.Pin_0, R2.Pin_1, Q2.C
  N3: J1.pin1, J2.pin1, J3.pin1, J4.pin1, M1.Pin_2, Q2.B, J5.GND
  N4: J1.pin2, J2.pin2, J3.pin2, J4.pin2, M1.Pin_1, 12V_LED_Array1.VCC, J5.PWR
  N5: M1.Pin_3, USB_C_Plug1.VCC
  N6: M1.Pin_4, USB_C_Plug1.GND
  N7: 12V_LED_Array1.GND, Q2.E

notes:
  Track should be broken between resistor connections
